# Fritzing sketch Arduino-prototype (saved by Fritzing 0.9.2b)
breadboards: 1

parts:
  Part1 = Arduino Uno (Rev3)
  LED1 = 7-SEGMENT-4DIGIT-YOUNGSUN [package=7-segment-4digit-youngsun]
  S1 = Pushbutton [package="[THT]"]
  S2 = Pushbutton [package="[THT]"]
  S3 = Pushbutton [package="[THT]"]
  S4 = Pushbutton [package="[THT]"]
  R1 = Resistor [tolerance=±5% resistance=220 package=THT]
  R3 = Resistor [tolerance=±5% resistance=10k package=THT]
  R4 = Resistor [tolerance=±5% resistance=10k package=THT]
  LED2 = LED - 5mm [color="Red (633nm)" package="5 mm [THT]"]
  J1 = Piezo Speaker
  R5 = Resistor [tolerance=±5% resistance=220 package=THT]

nets:
  N1: Part1.A0, LED1.E
  N2: Part1.A1, LED1.A
  N3: Part1.A2, LED1.B
  N4: Part1.A3, LED1.DIG2
  N5: Part1.A4/SDA, LED1.DIG3
  N6: Part1.A5/SCL, S2.Pin_2, S3.Pin_1, S3.Pin_2, S4.Pin_1, S4.Pin_2, R4.Pin_0
  N7: Part1.D8, LED1.G
  N8: Part1.D9_PWM, J1.pin2
  N9: Part1.D10_PWM/SS, R5.Pin_0
  N10: Part1.D11_PWM/MOSI, LED1.DIG1, LED1.COL-A
  N11: Part1.D12/MISO, LED1.COL-C
  N12: Part1.D13/SCK, LED2.anode
  N13: Part1.D2, S1.Pin_1, S1.Pin_2
  N14: Part1.D4, LED1.C
  N15: Part1.D5_PWM, LED1.D
  N16: Part1.D6_PWM, LED1.DIG4
  N17: Part1.D7, LED1.F
  N18: Part1.5V, S3.Pin_3, S3.Pin_4, R1.Pin_1, R3.Pin_1
  N19: Part1.GND, S1.Pin_3, S1.Pin_4, R4.Pin_1, LED2.cathode
  N20: S2.Pin_3, S2.Pin_4, R3.Pin_0
  N21: S4.Pin_4, R1.Pin_0
  N22: J1.pin1, R5.Pin_1
